# Fritzing sketch AC Sensor sketch (saved by Fritzing 0.9.3b)
breadboards: 1

parts:
  Componente1 = LCD1602-I2C
  Componente2 = Breadboard Power Supply Board SMD
  U1 = ESP32-38PinWide [part_number=ESP32-38PinWidev22]
  Componente3 = HX711 Weighing Sensor Module
  Load_Cell1 = Load Cell - Red/white/black/green
  U2 = TOUCH [package=touch1]

nets:
  GND: Componente1.GND, Componente2.GND, Componente3.GND
  VCC: Componente1.VCC, Componente2.VCC, Componente3.VCC
  N1: Componente1.SDA, U1.GPIO21
  N2: Componente1.SCL, U1.GPIO22
  N3: U1.GPIO15, U2.T1
  N4: U1.GPIO4, Componente3.CK/TX
  N5: U1.GPIO16, Componente3.DO/RX
  N6: Componente3.E+, Load_Cell1.wire1
  N7: Componente3.E-, Load_Cell1.wire3
  N8: Componente3.A+, Load_Cell1.wire2
  N9: Componente3.A-, Load_Cell1.wire4

notes:
  HX711 weighing module
  ESP32 board
  16x2 i2c LCD
  Breadboard power supply
  Touch sensor

custom parts:
  LCD1602-I2C: A standard character display, usually with 2x16 characters. Comes in many colors with LCM1602 IIC attached.
  ESP32-38PinWide: Generic 38-Pin ESP32 with wide format (only access to one side of pins on a breadboard) based on Stephen Lilley's HiLetgo ESP-WROOM-32 ESP32 ESP-32S Development Board.
  HX711 Weighing Sensor Module: HX711 is a precision 24-bit analog-to-digital converter (ADC) designed for weigh scales and industrial control applications to interface directly with a bridge sensor.
  Load Cell - Red/white/black/green: A rectangle load cell/weighting pressure Sensor with four wires - Red, white, black, green. Normally corresponding with E+, E-, A+, A- respectively.
